// Logisim project CPU_design.circ as structural Verilog: 1 circuit, main circuit main
module main (
);

  wire and_1_out, and_2_out, and_3_out, and_4_out, and_5_out, and_6_out, and_7_out, and_8_out, and_9_out,
       and_10_out, and_11_out, and_12_out, and_13_out, clock_1_out, clock_2_out, nor_1_out, not_1_out,
       not_2_out, not_3_out, not_4_out, not_5_out, or_1_out, or_2_out, or_3_out, or_4_out, or_5_out,
       or_6_out, xor_1_out, xor_2_out, xor_3_out, xor_4_out, xor_5_out, xor_6_out, xor_7_out, xor_8_out;
  wire [6:0] keyboard_1_data;
  wire [7:0] controlled_buffer_1_out, controlled_buffer_9_out, counter_1_q, register_1_q, register_2_q,
       register_3_q;
  wire [11:0] rom_1_data;

  Counter counter_1 (
    .load(or_1_out), .D(controlled_buffer_1_out), .count(not_1_out), .Q(counter_1_q), .clk(clock_1_out));  // open: carry, clr
  not not_1 (not_1_out, or_1_out);
  ROM #(.dataWidth(12)) rom_1 (.addr(counter_1_q), .data(rom_1_data), .sel(1'b1));
  not not_2 (not_2_out, rom_1_data[11]);
  assign controlled_buffer_1_out[0] = or_4_out ? rom_1_data[0] : 1'bz;  // Controlled_Buffer controlled_buffer_1
  assign controlled_buffer_1_out[1] = or_4_out ? rom_1_data[1] : 1'bz;  // Controlled_Buffer controlled_buffer_2
  assign controlled_buffer_1_out[2] = or_4_out ? rom_1_data[2] : 1'bz;  // Controlled_Buffer controlled_buffer_3
  assign controlled_buffer_1_out[3] = or_4_out ? rom_1_data[3] : 1'bz;  // Controlled_Buffer controlled_buffer_4
  not not_3 (not_3_out, rom_1_data[10]);
  not not_4 (not_4_out, rom_1_data[9]);
  assign controlled_buffer_1_out[4] = or_4_out ? rom_1_data[4] : 1'bz;  // Controlled_Buffer controlled_buffer_5
  assign controlled_buffer_1_out[5] = or_4_out ? rom_1_data[5] : 1'bz;  // Controlled_Buffer controlled_buffer_6
  assign controlled_buffer_1_out[6] = or_4_out ? rom_1_data[6] : 1'bz;  // Controlled_Buffer controlled_buffer_7
  assign controlled_buffer_1_out[7] = or_4_out ? rom_1_data[7] : 1'bz;  // Controlled_Buffer controlled_buffer_8
  not not_5 (not_5_out, rom_1_data[8]);
  Clock clock_1 (.out(clock_1_out));
  or or_1 (or_1_out, or_2_out, and_5_out);
  buf or_2 (or_2_out, and_3_out);  // OR_Gate
  and and_1 (and_1_out, not_5_out, not_4_out, not_3_out, not_2_out);
  and and_2 (and_2_out, rom_1_data[8], not_4_out, not_3_out, not_2_out);
  and and_3 (and_3_out, not_5_out, rom_1_data[9], not_3_out, not_2_out);
  and and_4 (and_4_out, rom_1_data[8], rom_1_data[9], not_3_out, not_2_out);
  and and_5 (and_5_out, or_3_out, 1'b1);
  buf or_3 (or_3_out, and_4_out);  // OR_Gate
  or or_4 (or_4_out, and_1_out, and_2_out, and_3_out, and_4_out);
  assign controlled_buffer_9_out[0] = 1'b0 ? controlled_buffer_1_out[0] : 1'bz;  // Controlled_Buffer controlled_buffer_9
  assign controlled_buffer_9_out[1] = 1'b0 ? controlled_buffer_1_out[1] : 1'bz;  // Controlled_Buffer controlled_buffer_10
  assign controlled_buffer_9_out[2] = 1'b0 ? controlled_buffer_1_out[2] : 1'bz;  // Controlled_Buffer controlled_buffer_11
  assign controlled_buffer_9_out[2] = 1'b0 ? and_11_out : 1'bz;  // Controlled_Buffer controlled_buffer_12
  assign controlled_buffer_9_out[1] = 1'b0 ? and_12_out : 1'bz;  // Controlled_Buffer controlled_buffer_13
  assign controlled_buffer_9_out[0] = 1'b0 ? and_13_out : 1'bz;  // Controlled_Buffer controlled_buffer_14
  assign controlled_buffer_9_out[3] = 1'b0 ? controlled_buffer_1_out[3] : 1'bz;  // Controlled_Buffer controlled_buffer_15
  assign controlled_buffer_9_out[4] = 1'b0 ? controlled_buffer_1_out[4] : 1'bz;  // Controlled_Buffer controlled_buffer_16
  assign controlled_buffer_9_out[5] = 1'b0 ? controlled_buffer_1_out[5] : 1'bz;  // Controlled_Buffer controlled_buffer_17
  assign controlled_buffer_9_out[6] = 1'b0 ? controlled_buffer_1_out[6] : 1'bz;  // Controlled_Buffer controlled_buffer_18
  assign controlled_buffer_9_out[6] = 1'b0 ? and_7_out : 1'bz;  // Controlled_Buffer controlled_buffer_19
  assign controlled_buffer_9_out[5] = 1'b0 ? and_8_out : 1'bz;  // Controlled_Buffer controlled_buffer_20
  assign controlled_buffer_9_out[4] = 1'b0 ? and_9_out : 1'bz;  // Controlled_Buffer controlled_buffer_21
  assign controlled_buffer_9_out[3] = 1'b0 ? and_10_out : 1'bz;  // Controlled_Buffer controlled_buffer_22
  assign controlled_buffer_9_out[7] = 1'b0 ? controlled_buffer_1_out[7] : 1'bz;  // Controlled_Buffer controlled_buffer_23
  assign controlled_buffer_9_out[7] = 1'b0 ? and_6_out : 1'bz;  // Controlled_Buffer controlled_buffer_24
  Register register_1 (.D(controlled_buffer_9_out), .en(1'b0), .Q(register_1_q), .clk(clock_2_out));  // open: clr
  and and_6 (and_6_out, register_1_q[7], controlled_buffer_1_out[7]);
  and and_7 (and_7_out, register_1_q[6], controlled_buffer_1_out[6]);
  and and_8 (and_8_out, register_1_q[5], controlled_buffer_1_out[5]);
  and and_9 (and_9_out, register_1_q[4], controlled_buffer_1_out[4]);
  and and_10 (and_10_out, register_1_q[3], controlled_buffer_1_out[3]);
  and and_11 (and_11_out, register_1_q[2], controlled_buffer_1_out[2]);
  and and_12 (and_12_out, register_1_q[1], controlled_buffer_1_out[1]);
  and and_13 (and_13_out, register_1_q[0], controlled_buffer_1_out[0]);
  Clock clock_2 (.out(clock_2_out));
  xor xor_1 (xor_1_out, register_1_q[7], controlled_buffer_1_out[7]);
  xor xor_2 (xor_2_out, register_1_q[6], controlled_buffer_1_out[6]);
  xor xor_3 (xor_3_out, register_1_q[5], controlled_buffer_1_out[5]);
  xor xor_4 (xor_4_out, register_1_q[4], controlled_buffer_1_out[4]);
  xor xor_5 (xor_5_out, register_1_q[3], controlled_buffer_1_out[3]);
  xor xor_6 (xor_6_out, register_1_q[2], controlled_buffer_1_out[2]);
  xor xor_7 (xor_7_out, register_1_q[1], controlled_buffer_1_out[1]);
  xor xor_8 (xor_8_out, register_1_q[0], controlled_buffer_1_out[0]);
  nor nor_1 (nor_1_out, xor_1_out, xor_2_out, xor_3_out, xor_4_out, xor_5_out, xor_6_out, xor_7_out, xor_8_out);
  buf or_5 (or_5_out, and_1_out);  // OR_Gate
  Hex_Digit_Display hex_digit_display_1 (.value(controlled_buffer_1_out[3:0]));  // open: dp
  Hex_Digit_Display hex_digit_display_2 (.value(controlled_buffer_1_out[7:4]));  // open: dp
  buf or_6 (or_6_out, and_2_out);  // OR_Gate
  Register register_2 (.D(controlled_buffer_1_out), .en(or_5_out), .Q(register_2_q), .clk(clock_1_out));  // open: clr
  Register register_3 (.D(controlled_buffer_1_out), .en(or_6_out), .Q(register_3_q), .clk(clock_1_out));  // open: clr
  assign controlled_buffer_1_out = 1'b0 ? {1'b0, keyboard_1_data} : 8'bz;  // Controlled_Buffer controlled_buffer_25
  TTY tty_1 (.data(register_2_q[6:0]), .clk(clock_1_out), .we(register_3_q[1]));  // open: clr
  Keyboard keyboard_1 (.clk(clock_1_out), .re(register_3_q[0]), .data(keyboard_1_data));  // open: clr, avail

  // Notes on the sheet:
  //   IP
  //   Program Memory
  //   contents of rom_1 (hex, n*v repeats v):
  //   102 4d 61 72 61 20 64 61 6a 20 64 65 63 6b 69 6d 61 20 64 6f 6e 65 73 69 20 6a 6f 73 20 6a 65 64 6e
  //   75 20 72 75 6e 64 75 20 6b 61 72 6c 6f 76 61 63 6b 6f 67 a a 100 300
  //   BUS to IP
  //   Equal BIT
  //   Literal to BUS
  //   Reg A
  //   Set IO1 TTY
  //   8bit DATA BUS
  //   KEYB to BUS
  //   Set IO2 Enable TTY (2) & KEY (1)
endmodule
